// Logisim project cpu.circ as structural Verilog: 4 circuits, main circuit CPU
module CPU (
);

  wire button_1_out, clock_1_out;
  wire [1:0] ram_1_data_2;
  wire [3:0] alu_1_s0, d_ff_1_q, d_ff_5_q, demultiplexer_1_out0, demultiplexer_1_out1, multiplexer_1_out,
       multiplexer_2_out, multiplexer_3_out;
  wire [15:0] counter_1_q, ram_1_data;

  Clock clock_1 (.out(clock_1_out));
  Button button_1 (.out(button_1_out));
  Counter #(.width(16), .max('hffff)) counter_1 (
    .Q(counter_1_q), .clk(clock_1_out), .clr(button_1_out));  // open: load, D, count, carry
  RAM #(.addrWidth(16), .dataWidth(16)) ram_1 (
    .addr(counter_1_q), .data({ram_1_data[15:12], ram_1_data_2[0], ram_1_data_2[1], ram_1_data[9:0]}));  // open: sel, clk, ld, clr
  D_Flip_Flop d_ff_1 (.clk(clock_1_out), .D(demultiplexer_1_out0[0]), .Q(d_ff_1_q[0]));  // open: Qn, preset, en, reset
  D_Flip_Flop d_ff_2 (.clk(clock_1_out), .D(demultiplexer_1_out0[1]), .Q(d_ff_1_q[1]));  // open: Qn, preset, en, reset
  D_Flip_Flop d_ff_3 (.clk(clock_1_out), .D(demultiplexer_1_out0[2]), .Q(d_ff_1_q[2]));  // open: Qn, preset, en, reset
  D_Flip_Flop d_ff_4 (.clk(clock_1_out), .D(demultiplexer_1_out0[3]), .Q(d_ff_1_q[3]));  // open: Qn, preset, en, reset
  Multiplexer #(.select(2), .width(4), .enable("false")) multiplexer_1 (
    .in0(d_ff_1_q), .in1(d_ff_5_q), .in2(ram_1_data[9:6]), .out(multiplexer_1_out), .sel(ram_1_data[3:2]));  // open: in3
  D_Flip_Flop d_ff_5 (.clk(clock_1_out), .D(demultiplexer_1_out1[0]), .Q(d_ff_5_q[0]));  // open: Qn, preset, en, reset
  D_Flip_Flop d_ff_6 (.clk(clock_1_out), .D(demultiplexer_1_out1[1]), .Q(d_ff_5_q[1]));  // open: Qn, preset, en, reset
  D_Flip_Flop d_ff_7 (.clk(clock_1_out), .D(demultiplexer_1_out1[2]), .Q(d_ff_5_q[2]));  // open: Qn, preset, en, reset
  D_Flip_Flop d_ff_8 (.clk(clock_1_out), .D(demultiplexer_1_out1[3]), .Q(d_ff_5_q[3]));  // open: Qn, preset, en, reset
  ALU alu_1 (
    .d0(ram_1_data[0]), .d1(ram_1_data[1]), .b3(multiplexer_1_out[3]), .b2(multiplexer_1_out[2]),
    .b1(multiplexer_1_out[1]), .b0(multiplexer_1_out[0]), .a3(multiplexer_2_out[3]),
    .a2(multiplexer_2_out[2]), .a1(multiplexer_2_out[1]), .a0(multiplexer_2_out[0]), .s3(alu_1_s0[3]),
    .s2(alu_1_s0[2]), .s1(alu_1_s0[1]), .s0(alu_1_s0[0]));  // open: c_out
  Multiplexer #(.select(2), .width(4), .enable("false")) multiplexer_2 (
    .in0(d_ff_1_q), .in1(d_ff_5_q), .in2(ram_1_data[9:6]), .in3(ram_1_data[9:6]), .out(multiplexer_2_out),
    .sel(ram_1_data[5:4]));
  Demultiplexer #(.width(4), .tristate("true"), .enable("false")) demultiplexer_1 (
    .out0(demultiplexer_1_out0), .out1(demultiplexer_1_out1), .in(multiplexer_3_out), .sel(ram_1_data[12]));
  Multiplexer #(.select(2), .width(4), .enable("false")) multiplexer_3 (
    .in0(d_ff_1_q), .in1(d_ff_5_q), .in2(ram_1_data[9:6]), .in3(alu_1_s0), .out(multiplexer_3_out),
    .sel(ram_1_data_2));
endmodule

// 4-bit ALU
module ALU (
  input  b3,
  input  b2,
  input  b1,
  input  b0,
  input  a3,
  input  a2,
  input  a1,
  input  a0,
  input  d0,
  input  d1,
  output c_out,
  output s3,
  output s2,
  output s1,
  output s0
);

  wire controller_1_out, controller_2_out, controller_3_out, controller_4_out, full_adder_2_cout,
       full_adder_3_cout, full_adder_4_cout;

  Controller controller_1 (.d1(d1), .d0(d0), .bi(b3), .out(controller_1_out));
  Full_Adder full_adder_1 (.cin(full_adder_2_cout), .x(a3), .y(controller_1_out), .Sum(s3), .cout(c_out));
  Controller controller_2 (.d1(d1), .d0(d0), .bi(b2), .out(controller_2_out));
  Full_Adder full_adder_2 (.cin(full_adder_3_cout), .x(a2), .y(controller_2_out), .Sum(s2), .cout(full_adder_2_cout));
  Controller controller_3 (.d1(d1), .d0(d0), .bi(b1), .out(controller_3_out));
  Full_Adder full_adder_3 (.cin(full_adder_4_cout), .x(a1), .y(controller_3_out), .Sum(s1), .cout(full_adder_3_cout));
  Controller controller_4 (.d1(d1), .d0(d0), .bi(b0), .out(controller_4_out));
  Full_Adder full_adder_4 (.cin(d0), .x(a0), .y(controller_4_out), .Sum(s0), .cout(full_adder_4_cout));

  // Notes on the sheet:
  //   x3
  //   x2
  //   x1
  //   x0
endmodule

// FA
module Full_Adder (
  input  cin,
  input  x,
  input  y,
  output Sum,
  output cout
);

  wire and_1_out, and_2_out, xor_1_out;

  and and_1 (and_1_out, x, y);
  xor xor_1 (xor_1_out, x, y);
  and and_2 (and_2_out, cin, xor_1_out);
  xor xor_2 (Sum, cin, xor_1_out);
  or or_1 (cout, and_2_out, and_1_out);

  // Notes on the sheet:
  //   Full Adder
endmodule

module Controller (
  input  d1,
  input  d0,
  input  bi,
  output out
);

  wire and_1_out, and_2_out, and_3_out, not_1_out, not_2_out, not_3_out;

  not not_1 (not_1_out, d0);
  and and_1 (and_1_out, d1, not_1_out);
  not not_2 (not_2_out, bi);
  not not_3 (not_3_out, d1);
  and and_2 (and_2_out, d0, not_3_out, not_2_out);
  or or_1 (out, and_1_out, and_2_out, and_3_out);
  and and_3 (and_3_out, bi, not_1_out);
endmodule
